// Logisim project problem_set.circ as structural Verilog: 5 circuits, main circuit main
module main (
);


  // Notes on the sheet:
  //   1. negator
  //   2.bit_adder
  //   4.bit_finder
  //   თქვენი ამოცანაა შეასრულოთ მოცემული წრედები
  //   3. priority_encoder
  //   თითოეულ წრედს აქვს Logisim-ექვივალენტური ჩაშენებული წრედი.
  //   ჩაშენებული წრედის შედეგს.
  //   ამოცანის დასაწყებად ამოშალეთ შუა built-in წრედი და შეავსეთ თქვენი ლოგიკით.
  //   კითხვების შემთხვევაში მომწერეთ ან დასვით კითხვა კლასრუმზე.
  //   დაგეწერებათ სრული ქულა იმ შემთხვევაში თუ თქვენი წრედის შედეგი ყოველთვის ემთხვევა
endmodule

module _1__negator (
  input  [7:0] in_1,
  output [7:0] out_2
);

  Negator negator_1 (.in(in_1), .out(out_2));

  // Notes on the sheet:
  //   აქ არ გამოიყენოთ subtractor და multiplier-ჩაშენებული წრედები.
endmodule

module _2__bit_adder (
  input  [7:0] in_1,
  output [3:0] out_2
);

  BitAdder bitadder_1 (.in0(in_1), .out(out_2));
endmodule

module _3__priority_encoder (
  input  in_1,
  input  in_2,
  input  in_3,
  input  in_4,
  input  in_5,
  input  in_6,
  input  in_7,
  input  in_8,
  output [2:0] out_9,
  output out_10
);

  Priority_Encoder priority_encoder_1 (
    .in0(in_1), .in1(in_2), .in2(in_3), .in3(in_4), .in4(in_5), .in5(in_6), .in6(in_7), .in7(in_8),
    .out(out_9), .gs(out_10));  // open: en_in, en_out

  // Notes on the sheet:
  //   ამოცანის წონის ნახევარს მაინც მიიღებთ.
  //   ამ წრედის ასაწყობად არ გამოიყენოთ bitfinder Built-in წრედი.
  //   შეგიძლიათ გამოიყენოთ მხოლოდ თქვენი დაწერილი bit_finder-ი.
  //   თუ ვერ ამოხსენით bit_finder-ი და სხვა გზა არ გაქვთ, ამოხსნილი 
endmodule

module _4__bit_finder (
  input  [7:0] in_1,
  output [2:0] out_2,
  output out_3
);

  BitFinder bitfinder_1 (.in(in_1), .index(out_2), .found(out_3));

  // Notes on the sheet:
  //   ამოცანის წონის ნახევარს მაინც მიიღებთ.
  //   ამ წრედის ასაწყობად არ გამოიყენოთ priority_encoder Built-in წრედი.
  //   შეგიძლიათ გამოიყენოთ მხოლოდ თქვენი დაწერილი priority_encoder-ი.
  //   თუ ვერ ამოხსენით priority_encoder-ი და სხვა გზა არ გაქვთ, ამოხსნილი 
endmodule
