// Logisim project mul_signed.circ as structural Verilog: 10 circuits, main circuit main
module main (
  input  in_1,
  input  in_2
);

  wire and_1_out, and_2_out, or_1_out, undriven, undriven_2;

  Clock clock_1 ();  // open: out
  not not_1 (in_1, in_1);
  or or_1 (or_1_out, in_2, undriven);
  buf and_1 (and_1_out, in_2);  // AND_Gate
  and and_2 (and_2_out, undriven_2, in_2);
endmodule

module mul_8_signed (
  input  [7:0] Input_A,
  input  [7:0] Input_B,
  output [7:0] Output
);

  wire [7:7] mul_8_1_output;

  mul_8 mul_8_1 (
    .Input_A({1'b0, Input_A[6:0]}), .Input_B({1'b0, Input_B[6:0]}), .Output({mul_8_1_output[7], Output[6:0]}));
  sign_decider sign_decider_1 (.in_1(Input_B), .in_2(Input_A), .out_3(Output[7]));
endmodule

module sign_decider (
  input  [7:0] in_1,
  input  [7:0] in_2,
  output out_3
);

  wire nor_1_out, nor_2_out, not_1_out, or_1_out, xor_1_out;

  nor nor_1 (nor_1_out, in_1[0], in_1[1], in_1[2], in_1[3], in_1[4], in_1[5], in_1[6], in_1[7]);
  nor nor_2 (nor_2_out, in_2[0], in_2[1], in_2[2], in_2[3], in_2[4], in_2[5], in_2[6], in_2[7]);
  or or_1 (or_1_out, nor_1_out, nor_2_out);
  xor xor_1 (xor_1_out, in_1[7], in_2[7]);
  not not_1 (not_1_out, or_1_out);
  Multiplexer #(.enable("false")) multiplexer_1 (.in0(not_1_out), .in1(xor_1_out), .out(out_3), .sel(not_1_out));

  // Notes on the sheet:
  //   sign If not zero
  //   IsZero?
endmodule

module vec_8_8_8_add (
  input  [7:0] Input_A,
  input  [7:0] Input_A_2,
  input  [7:0] Input_A_3,
  input  [7:0] Input_A_4,
  input  [7:0] Input_A_5,
  input  [7:0] Input_A_6,
  input  [7:0] Input_A_7,
  input  [7:0] Input_A_8,
  input  [7:0] Input_B,
  input  [7:0] Input_B_2,
  input  [7:0] Input_B_3,
  input  [7:0] Input_B_4,
  input  [7:0] Input_B_5,
  input  [7:0] Input_B_6,
  input  [7:0] Input_B_7,
  input  [7:0] Input_B_8,
  output [7:0] Output_C,
  output [7:0] Output_C_2,
  output [7:0] Output_C_3,
  output [7:0] Output_C_4,
  output [7:0] Output_C_5,
  output [7:0] Output_C_6,
  output [7:0] Output_C_7,
  output [7:0] Output_C_8
);

  Adder adder_1 (.a(Input_A), .b(Input_B), .out(Output_C));  // open: cin, cout
  Adder adder_2 (.a(Input_A_2), .b(Input_B_2), .out(Output_C_2));  // open: cin, cout
  Adder adder_3 (.a(Input_A_3), .b(Input_B_3), .out(Output_C_3));  // open: cin, cout
  Adder adder_4 (.a(Input_A_4), .b(Input_B_4), .out(Output_C_4));  // open: cin, cout
  Adder adder_5 (.a(Input_A_5), .b(Input_B_5), .out(Output_C_5));  // open: cin, cout
  Adder adder_6 (.a(Input_A_6), .b(Input_B_6), .out(Output_C_6));  // open: cin, cout
  Adder adder_7 (.a(Input_A_7), .b(Input_B_7), .out(Output_C_7));  // open: cin, cout
  Adder adder_8 (.a(Input_A_8), .b(Input_B_8), .out(Output_C_8));  // open: cin, cout
endmodule

module vec_8_8_8_mul (
  input  [7:0] Input_A,
  input  [7:0] Input_A_2,
  input  [7:0] Input_A_3,
  input  [7:0] Input_A_4,
  input  [7:0] Input_A_5,
  input  [7:0] Input_A_6,
  input  [7:0] Input_A_7,
  input  [7:0] Input_A_8,
  input  [7:0] Input_B,
  input  [7:0] Input_B_2,
  input  [7:0] Input_B_3,
  input  [7:0] Input_B_4,
  input  [7:0] Input_B_5,
  input  [7:0] Input_B_6,
  input  [7:0] Input_B_7,
  input  [7:0] Input_B_8,
  output [7:0] Outpub_C,
  output [7:0] Outpub_C_2,
  output [7:0] Outpub_C_3,
  output [7:0] Outpub_C_4,
  output [7:0] Outpub_C_5,
  output [7:0] Outpub_C_6,
  output [7:0] Outpub_C_7,
  output [7:0] Outpub_C_8
);

  Multiplier multiplier_1 (.a(Input_A), .b(Input_B), .out(Outpub_C));  // open: cin, cout
  Multiplier multiplier_2 (.a(Input_A_2), .b(Input_B_2), .out(Outpub_C_2));  // open: cin, cout
  Multiplier multiplier_3 (.a(Input_A_3), .b(Input_B_3), .out(Outpub_C_3));  // open: cin, cout
  Multiplier multiplier_4 (.a(Input_A_4), .b(Input_B_4), .out(Outpub_C_4));  // open: cin, cout
  Multiplier multiplier_5 (.a(Input_A_5), .b(Input_B_5), .out(Outpub_C_5));  // open: cin, cout
  Multiplier multiplier_6 (.a(Input_A_6), .b(Input_B_6), .out(Outpub_C_6));  // open: cin, cout
  Multiplier multiplier_7 (.a(Input_A_7), .b(Input_B_7), .out(Outpub_C_7));  // open: cin, cout
  Multiplier multiplier_8 (.a(Input_A_8), .b(Input_B_8), .out(Outpub_C_8));  // open: cin, cout
endmodule

module mat_mul (
  input  [7:0] a11,
  input  [7:0] a12,
  input  [7:0] a21,
  input  [7:0] a22,
  input  [7:0] b11,
  input  [7:0] b12,
  input  [7:0] b21,
  input  [7:0] b22,
  output [7:0] c11,
  output [7:0] c12,
  output [7:0] c21,
  output [7:0] c22
);

  vec_8_2_mul vec_8_2_mul_1 (.in_1(a11), .in_2(a12), .in_3(b11), .in_4(b21), .out_5(c11));
  vec_8_2_mul vec_8_2_mul_2 (.in_1(a11), .in_2(a12), .in_3(b12), .in_4(b22), .out_5(c12));
  vec_8_2_mul vec_8_2_mul_3 (.in_1(a21), .in_2(a22), .in_3(b11), .in_4(b21), .out_5(c21));
  vec_8_2_mul vec_8_2_mul_4 (.in_1(a11), .in_2(a12), .in_3(b12), .in_4(b22), .out_5(c22));
endmodule

module vec_8_2_mul (
  input  [7:0] in_1,
  input  [7:0] in_2,
  input  [7:0] in_3,
  input  [7:0] in_4,
  output [7:0] out_5
);

  wire [7:0] multiplier_1_out, multiplier_2_out;

  Multiplier multiplier_1 (.a(in_1), .b(in_3), .out(multiplier_1_out));  // open: cin, cout
  Multiplier multiplier_2 (.a(in_2), .b(in_4), .out(multiplier_2_out));  // open: cin, cout
  Adder adder_1 (.a(multiplier_1_out), .b(multiplier_2_out), .out(out_5));  // open: cin, cout
endmodule

module vec_8_2_add (
  input  [7:0] in_1,
  input  [7:0] in_2,
  input  [7:0] in_3,
  input  [7:0] in_4,
  output [7:0] out_5,
  output [7:0] out_6
);

  Adder adder_1 (.a(in_1), .b(in_3), .out(out_5));  // open: cin, cout
  Adder adder_2 (.a(in_2), .b(in_4), .out(out_6));  // open: cin, cout
endmodule

module mul_int8 (
  input  [7:0] Input_A,
  input  [7:0] Input_B,
  output [7:0] Output
);

  mul_8 mul_8_1 (.Input_A(Input_A), .Input_B(Input_B), .Output(Output));
endmodule

module mat_mul_2by2 (
  input  [7:0] in_1,
  input  [7:0] in_2,
  input  [7:0] in_3,
  input  [7:0] in_4,
  input  [7:0] in_5,
  input  [7:0] in_6,
  input  [7:0] in_7,
  input  [7:0] in_8,
  input  [7:0] in_9,
  input  [7:0] in_10,
  input  [7:0] in_11,
  input  [7:0] in_12
);

  vec_8_2_mul vec_8_2_mul_1 (.in_1(in_1), .in_2(in_2), .in_3(in_7), .in_4(in_11), .out_5(in_5));
  vec_8_2_mul vec_8_2_mul_2 (.in_1(in_1), .in_2(in_2), .in_3(in_8), .in_4(in_12), .out_5(in_6));
  vec_8_2_mul vec_8_2_mul_3 (.in_1(in_3), .in_2(in_4), .in_3(in_7), .in_4(in_11), .out_5(in_9));
  vec_8_2_mul vec_8_2_mul_4 (.out_5(in_10));  // open: in_1, in_2, in_3, in_4
endmodule
