// Logisim project multiplication.circ as structural Verilog: 5 circuits, main circuit main
module main (
);

  mul_8 mul_8_1 ();  // open: Input_A, Input_B, Output
endmodule

module shifter (
  input  [7:0] in_1,
  output [7:0] out_2
);


  assign out_2 = {in_1[6:0], 1'b0};
endmodule

module multiply_bit (
  input  [7:0] in_1,
  input  in_2,
  output [7:0] shifted,
  output [7:0] multiplied
);

  Multiplexer #(.width(8)) multiplexer_1 (.in0({8{1'b0}}), .in1(in_1), .out(multiplied), .sel(in_2));  // open: en
  shifter shifter_1 (.in_1(in_1), .out_2(shifted));
endmodule

module mul_8 (
  input  [7:0] Input_A,
  input  [7:0] Input_B,
  output [7:0] Output
);

  wire [7:0] multiply_bit_1_multiplied, multiply_bit_1_shifted, multiply_bit_2_multiplied,
       multiply_bit_2_shifted, multiply_bit_3_multiplied, multiply_bit_3_shifted, multiply_bit_4_multiplied,
       multiply_bit_4_shifted, multiply_bit_5_multiplied, multiply_bit_5_shifted, multiply_bit_6_multiplied,
       multiply_bit_6_shifted, multiply_bit_7_multiplied, multiply_bit_7_shifted, multiply_bit_8_multiplied;

  multiply_bit multiply_bit_1 (
    .in_1(Input_A), .in_2(Input_B[0]), .shifted(multiply_bit_1_shifted),
    .multiplied(multiply_bit_1_multiplied));
  multiply_bit multiply_bit_2 (
    .in_1(multiply_bit_1_shifted), .in_2(Input_B[1]), .shifted(multiply_bit_2_shifted),
    .multiplied(multiply_bit_2_multiplied));
  multiply_bit multiply_bit_3 (
    .in_1(multiply_bit_6_shifted), .in_2(Input_B[4]), .shifted(multiply_bit_3_shifted),
    .multiplied(multiply_bit_3_multiplied));
  multiply_bit multiply_bit_4 (
    .in_1(multiply_bit_3_shifted), .in_2(Input_B[5]), .shifted(multiply_bit_4_shifted),
    .multiplied(multiply_bit_4_multiplied));
  multiply_bit multiply_bit_5 (
    .in_1(multiply_bit_2_shifted), .in_2(Input_B[2]), .shifted(multiply_bit_5_shifted),
    .multiplied(multiply_bit_5_multiplied));
  multiply_bit multiply_bit_6 (
    .in_1(multiply_bit_5_shifted), .in_2(Input_B[3]), .shifted(multiply_bit_6_shifted),
    .multiplied(multiply_bit_6_multiplied));
  multiply_bit multiply_bit_7 (
    .in_1(multiply_bit_4_shifted), .in_2(Input_B[6]), .shifted(multiply_bit_7_shifted),
    .multiplied(multiply_bit_7_multiplied));
  multiply_bit multiply_bit_8 (
    .in_1(multiply_bit_7_shifted), .in_2(Input_B[7]), .multiplied(multiply_bit_8_multiplied));  // open: shifted
  add_8_8 add_8_8_1 (
    .in_1(multiply_bit_1_multiplied), .in_2(multiply_bit_2_multiplied), .in_3(multiply_bit_5_multiplied),
    .in_4(multiply_bit_6_multiplied), .in_5(multiply_bit_3_multiplied), .in_6(multiply_bit_4_multiplied),
    .in_7(multiply_bit_7_multiplied), .in_8(multiply_bit_8_multiplied), .out_9(Output));
endmodule

module add_8_8 (
  input  [7:0] in_1,
  input  [7:0] in_2,
  input  [7:0] in_3,
  input  [7:0] in_4,
  input  [7:0] in_5,
  input  [7:0] in_6,
  input  [7:0] in_7,
  input  [7:0] in_8,
  output [7:0] out_9
);

  wire [7:0] adder_1_out, adder_2_out, adder_3_out, adder_4_out, adder_5_out, adder_6_out;

  Adder adder_1 (.a(in_1), .b(in_2), .out(adder_1_out));  // open: cin, cout
  Adder adder_2 (.a(in_3), .b(in_4), .out(adder_2_out));  // open: cin, cout
  Adder adder_3 (.a(in_5), .b(in_6), .out(adder_3_out));  // open: cin, cout
  Adder adder_4 (.a(in_7), .b(in_8), .out(adder_4_out));  // open: cin, cout
  Adder adder_5 (.a(adder_1_out), .b(adder_2_out), .out(adder_5_out));  // open: cin, cout
  Adder adder_6 (.a(adder_3_out), .b(adder_4_out), .out(adder_6_out));  // open: cin, cout
  Adder adder_7 (.a(adder_5_out), .b(adder_6_out), .out(out_9));  // open: cin, cout
endmodule
