// Logisim project scott_alu.circ as structural Verilog: 5 circuits, main circuit main
module main (
  input  in_1,
  input  in_2,
  output out_3
);

  wire nor_2_out;

  nor nor_1 (out_3, in_1, nor_2_out);
  nor nor_2 (nor_2_out, out_3, in_2);
endmodule

module Scott_ALU (
  input  [15:0] A,
  input  [15:0] B,
  input  Carry_in,
  input  [2:0] op,
  output [15:0] out_5,
  output Carry_out,
  output A_larger,
  output Equal,
  output Output_zero
);

  wire adder_1_cout, bitselector_1_out;
  wire [15:0] adder_1_out, and_1_out, not_1_out, or_1_out, shifter_1_out, shifter_2_out, xor_1_out;

  Adder #(.width(16)) adder_1 (.a(B), .b(A), .out(adder_1_out), .cin(Carry_in), .cout(adder_1_cout));
  BitSelector #(.width(16)) bitselector_1 (.in(A), .out(bitselector_1_out), .sel(4'b1111));
  Shifter #(.width(16), .shift("lr")) shifter_1 (.in(A), .\dist (4'b0001), .out(shifter_1_out));
  assign not_1_out = ~A;  // NOT_Gate not_1, 16 bits wide
  assign and_1_out = A & B;  // AND_Gate and_1, 16 bits wide
  assign or_1_out = A | B;  // OR_Gate or_1, 16 bits wide
  assign xor_1_out = A ^ B;  // XOR_Gate xor_1, 16 bits wide
  Comparator #(.width(16)) comparator_1 (.a(A), .b(B), .gt(A_larger), .eq(Equal));  // open: lt
  Shifter #(.width(16)) shifter_2 (.in(A), .\dist (4'b0001), .out(shifter_2_out));
  Multiplexer #(.select(3), .width(16), .enable("false")) multiplexer_1 (
    .in0(adder_1_out), .in1({shifter_2_out[15:1], Carry_in}), .in2({Carry_in, shifter_1_out[14:0]}),
    .in3(not_1_out), .in4(and_1_out), .in5(or_1_out), .in6(xor_1_out), .out(out_5), .sel(op));  // open: in7
  or or_2 (Carry_out, adder_1_cout, bitselector_1_out);
  Comparator #(.width(16)) comparator_2 (.a(out_5), .b({16{1'b0}}), .eq(Output_zero));  // open: gt, lt
endmodule

module Scott_ALU_unfinished (
  input  [15:0] A,
  input  [15:0] B,
  input  Carry_in,
  input  [2:0] op,
  output [15:0] Output,
  output Carry_out,
  output A_larger,
  output Equal,
  output Output_zero
);

  Shifter #(.shift("lr")) shifter_1 ();  // open: in, dist, out
  Shifter shifter_2 ();  // open: in, dist, out
endmodule

module joystick_sample (
  input  [3:0] in_1,
  input  [3:0] in_2,
  output [6:0] out_3
);

  wire clock_1_out;

  Hex_Digit_Display hex_digit_display_1 ();  // open: value, dp
  Clock clock_1 (.out(clock_1_out));
  TTY tty_1 (.data(out_3), .clk(clock_1_out));  // open: we, clr
  Keyboard keyboard_1 (.clk(clock_1_out), .data(out_3));  // open: re, clr, avail
  _7_Segment_Display u_7_segment_display_1 (
    .g(in_1[3]), .f(in_1[2]), .a(in_1[1]), .b(in_1[0]), .e(in_2[3]), .d(in_2[2]), .c(in_2[1]), .dp(in_2[0]));
endmodule

module BFD (
  input  [3:0] in_1,
  input  [3:0] in_2
);

  wire [15:0] decoder_1_out15;

  Decoder #(.select(4)) decoder_1 (
    .out0(decoder_1_out15[15]), .out1(decoder_1_out15[14]), .out2(decoder_1_out15[13]),
    .out3(decoder_1_out15[12]), .out4(decoder_1_out15[11]), .out5(decoder_1_out15[10]),
    .out6(decoder_1_out15[9]), .out7(decoder_1_out15[8]), .out8(decoder_1_out15[7]),
    .out9(decoder_1_out15[6]), .out10(decoder_1_out15[5]), .out11(decoder_1_out15[4]),
    .out12(decoder_1_out15[3]), .out13(decoder_1_out15[2]), .out14(decoder_1_out15[1]),
    .out15(decoder_1_out15[0]), .sel(in_1));  // open: en
  Demultiplexer #(.select(4), .width(16), .enable("false")) demultiplexer_1 (
    .in(decoder_1_out15), .sel(in_2));  // open: out0, out1, out2, out3, out4, out5, out6, out7, out8, out9, out10, out11, out12, out13, out14, out15
endmodule
