// Logisim project flip_flops.circ as structural Verilog: 7 circuits, main circuit main
module main (
  input  Reset,
  input  Enable,
  input  Set,
  input  Reset_2,
  input  Enable_2,
  input  Set_2,
  output State,
  output Not_State,
  output State_2,
  output Not_State_2
);

  wire and_1_out, and_2_out, and_3_out, and_4_out;

  Clock clock_1 ();  // open: out
  and and_1 (and_1_out, Reset, Enable);
  and and_2 (and_2_out, Enable, Set);
  and and_3 (and_3_out, State_2, Reset_2, Enable_2);
  and and_4 (and_4_out, Enable_2, Set_2, Not_State_2);
  nor nor_1 (State, and_1_out, Not_State);
  nor nor_2 (Not_State, State, and_2_out);
  nor nor_3 (State_2, and_3_out, Not_State_2);
  nor nor_4 (Not_State_2, State_2, and_4_out);
endmodule

module jk_ff (
  input  Reset,
  input  Enable,
  input  Set,
  input  Async_Reset,
  input  Async_Set,
  output State,
  output Not_State
);

  wire and_1_out, and_2_out;

  and and_1 (and_1_out, State, Reset, Enable);
  and and_2 (and_2_out, Enable, Set, Not_State);
  nor nor_1 (State, and_1_out, ~Async_Reset, Not_State);  // NOR_Gate
  nor nor_2 (Not_State, State, Async_Set, and_2_out);
endmodule

module d_latch (
  input  Enable,
  input  D,
  output Output
);

  wire and_1_out, and_2_out, nor_2_out, not_1_out;

  not not_1 (not_1_out, D);
  and and_1 (and_1_out, not_1_out, Enable);
  and and_2 (and_2_out, Enable, D);
  nor nor_1 (Output, and_1_out, nor_2_out);
  nor nor_2 (nor_2_out, Output, and_2_out);
endmodule

module d_ff_v1 (
  input  in_1,
  input  in_2,
  output out_3
);

  wire and_1_out, and_2_out, and_3_out, nor_2_out, not_1_out, not_2_out;

  and and_1 (and_1_out, in_1, not_1_out);
  not not_1 (not_1_out, in_1);
  not not_2 (not_2_out, in_2);
  and and_2 (and_2_out, not_2_out, and_1_out);
  and and_3 (and_3_out, and_1_out, in_2);
  nor nor_1 (out_3, and_2_out, nor_2_out);
  nor nor_2 (nor_2_out, out_3, and_3_out);
endmodule

module d_ff_v2 (
  input  in_1,
  input  in_2,
  output out_3
);

  wire and_1_out, and_2_out, and_3_out, nor_2_out, not_1_out, not_2_out, not_3_out, not_4_out;

  not not_1 (not_1_out, not_3_out);
  not not_2 (not_2_out, in_1);
  not not_3 (not_3_out, not_2_out);
  not not_4 (not_4_out, in_2);
  and and_1 (and_1_out, in_1, not_1_out);
  and and_2 (and_2_out, not_4_out, and_1_out);
  and and_3 (and_3_out, and_1_out, in_2);
  nor nor_1 (out_3, and_2_out, nor_2_out);
  nor nor_2 (nor_2_out, out_3, and_3_out);
endmodule

module sr_latch (
  input  Reset,
  input  Enable,
  input  Set,
  output State,
  output Not_State
);

  wire and_1_out, and_2_out;

  and and_1 (and_1_out, Reset, Enable);
  and and_2 (and_2_out, Enable, Set);
  nor nor_1 (State, and_1_out, Not_State);
  nor nor_2 (Not_State, State, and_2_out);
endmodule

module sr_latch_2 (
  input  Reset,
  input  Set,
  output State,
  output Not_State
);

  nor nor_1 (State, Reset, Not_State);
  nor nor_2 (Not_State, State, Set);
endmodule
