// Logisim project seminary_3.circ as structural Verilog: 9 circuits, main circuit main
module main (
);

  T_Flip_Flop t_ff_1 ();  // open: clk, T, Q, Qn, preset, reset, en
  Counter counter_1 ();  // open: load, D, count, Q, carry, clk, clr
  D_Flip_Flop d_ff_1 ();  // open: clk, D, Q, Qn, preset, en, reset
  Shift_Register shift_register_1 ();  // open: shift, in, clk, out, load, clr, d0, q0, d1, q1, d2, q2, d3, q3, d4, q4, d5, q5, d6, q6, d7, q7
endmodule

module dff_01 (
  input  Reset,
  input  Set,
  input  Async_Reset,
  output Q,
  output Not_Q
);

  nor nor_1 (Q, Reset, Async_Reset, Not_Q);
  nor nor_2 (Not_Q, Q, Set);
endmodule

module dff_02 (
  input  Enable,
  input  D,
  input  in_3,
  output out_4
);

  wire and_1_out, and_2_out, not_1_out;

  not not_1 (not_1_out, D);
  and and_1 (and_1_out, not_1_out, Enable);
  and and_2 (and_2_out, Enable, D);
  dff_01 dff_01_1 (.Reset(and_1_out), .Set(and_2_out), .Async_Reset(in_3), .Q(out_4));  // open: Not_Q
endmodule

module dff_03 (
  input  Clock,
  input  D,
  input  Reset,
  output out_4
);

  wire and_1_out, not_1_out, not_2_out, not_3_out;

  not not_1 (not_1_out, not_3_out);
  not not_2 (not_2_out, not_1_out);
  not not_3 (not_3_out, Clock);
  dff_02 dff_02_1 (.Enable(and_1_out), .D(D), .in_3(Reset), .out_4(out_4));
  and and_1 (and_1_out, Clock, not_2_out);
endmodule

module tff_from_dff (
  input  T,
  input  Async_Reset,
  input  CLK,
  output Q
);

  wire multiplexer_1_out, not_1_out;

  Multiplexer multiplexer_1 (.in0(Q), .in1(not_1_out), .out(multiplexer_1_out), .sel(T));  // open: en
  not not_1 (not_1_out, Q);
  dff_03 dff_03_1 (.Clock(CLK), .D(multiplexer_1_out), .out_4(Q), .Reset(Async_Reset));
endmodule

module shift_reg (
  input  Clk,
  input  Load,
  input  Reset,
  input  Input,
  input  in_5,
  input  in_6
);

  wire register_from_dff_1_output, register_from_dff_2_output, register_from_dff_3_output,
       register_from_dff_4_output, register_from_dff_5_output;

  Shift_Register shift_register_1 (
    .in(in_5), .clk(in_6));  // open: shift, out, load, clr, d0, q0, d1, q1, d2, q2, d3, q3, d4, q4, d5, q5, d6, q6, d7, q7
  register_from_dff register_from_dff_1 (
    .Input(register_from_dff_2_output), .Reset(Reset), .Output(register_from_dff_1_output), .Load(Load),
    .Clk(Clk));
  register_from_dff register_from_dff_2 (
    .Input(Input), .Reset(Reset), .Output(register_from_dff_2_output), .Load(Load), .Clk(Clk));
  register_from_dff register_from_dff_3 (
    .Input(register_from_dff_1_output), .Reset(Reset), .Output(register_from_dff_3_output), .Load(Load),
    .Clk(Clk));
  register_from_dff register_from_dff_4 (
    .Input(register_from_dff_3_output), .Reset(Reset), .Output(register_from_dff_4_output), .Load(Load),
    .Clk(Clk));
  register_from_dff register_from_dff_5 (
    .Input(register_from_dff_4_output), .Reset(Reset), .Output(register_from_dff_5_output), .Load(Load),
    .Clk(Clk));
endmodule

module register_from_dff (
  input  Load,
  input  Input,
  input  Reset,
  input  Clk,
  output Output
);

  wire multiplexer_1_out;

  Multiplexer multiplexer_1 (.in0(Output), .in1(Input), .out(multiplexer_1_out), .sel(Load));  // open: en
  dff_03 dff_03_1 (.Clock(Clk), .D(multiplexer_1_out), .out_4(Output), .Reset(Reset));
endmodule

module reg_8 (
  input  [7:0] in_1,
  input  Clk,
  input  Load,
  input  Reset,
  output [7:0] out_5
);

  register_from_dff register_from_dff_1 (.Input(in_1[0]), .Reset(Reset), .Output(out_5[0]), .Load(Load), .Clk(Clk));
  register_from_dff register_from_dff_2 (.Input(in_1[1]), .Reset(Reset), .Output(out_5[1]), .Load(Load), .Clk(Clk));
  register_from_dff register_from_dff_3 (.Input(in_1[2]), .Reset(Reset), .Output(out_5[2]), .Load(Load), .Clk(Clk));
  register_from_dff register_from_dff_4 (.Input(in_1[3]), .Reset(Reset), .Output(out_5[3]), .Load(Load), .Clk(Clk));
  register_from_dff register_from_dff_5 (.Input(in_1[4]), .Reset(Reset), .Output(out_5[4]), .Load(Load), .Clk(Clk));
  register_from_dff register_from_dff_6 (.Input(in_1[5]), .Reset(Reset), .Output(out_5[5]), .Load(Load), .Clk(Clk));
  register_from_dff register_from_dff_7 (.Input(in_1[6]), .Reset(Reset), .Output(out_5[6]), .Load(Load), .Clk(Clk));
  register_from_dff register_from_dff_8 (.Input(in_1[7]), .Reset(Reset), .Output(out_5[7]), .Load(Load), .Clk(Clk));
endmodule

module counter_8 (
  input  Clk,
  input  Inc,
  input  Reset,
  output [7:0] out_4
);

  wire [7:0] adder_1_out, multiplexer_1_out;

  Adder adder_1 (.a(out_4), .b(8'h1), .out(adder_1_out));  // open: cin, cout
  Multiplexer #(.width(8)) multiplexer_1 (
    .in0(out_4), .in1(adder_1_out), .out(multiplexer_1_out), .sel(Inc));  // open: en
  reg_8 reg_8_1 (.Clk(Clk), .Load(Inc), .Reset(Reset), .in_1(multiplexer_1_out), .out_5(out_4));
endmodule
