// Logisim project shifter.circ as structural Verilog
module multiflayer (
  input  [7:0] in_1,
  input  in_2,
  input  [7:0] in_3,
  output [7:0] out_4
);
endmodule

module shift (
  input  in_1,
  input  [7:0] in_2,
  input  [7:0] in_3
);


  assign in_3 = {in_2[6:0], in_1};
endmodule

module mul_1 (
  input  [7:0] in_1,
  input  in_2,
  input  [7:0] in_3
);

  shift shift_1 ();  // open: in_2, in_3, in_1
endmodule
